// Logisim project ALU.circ as structural Verilog: 36 circuits, main circuit Ida ALU
// ALU
module Ida_ALU (
  input  [23:0] ALU_Source_1,
  input  [23:0] ALU_Source_2,
  input  [3:0] Operation,
  output [23:0] ALU_Result
);

  wire [23:0] _14_result, _15_result, add1_result, add2_result, add_result, and_result, or_result, rl_result,
       rr_result, scomp_result, sll_result, sra_result, srl_result, sub_result, ucomp_result, xor_result;

  // Probe on ALU_Source_1
  // Probe on ALU_Source_2
  // Probe on Operation
  // Probe on ALU_Result
  Shift_Left_Logical SLL (.in_1(ALU_Source_1), .in_2(ALU_Source_2), .out_3(sll_result));
  Shift_Right_Logical SRL (.Source_1(ALU_Source_1), .Source_2(ALU_Source_2), .out_3(srl_result));
  Shift_Right_Arithmetic SRA (.Source_1(ALU_Source_1), .Source_2(ALU_Source_2), .out_3(sra_result));
  Rotate_Left RL (.Source_1(ALU_Source_1), .Source_2(ALU_Source_2), .out_3(rl_result));
  Rotate_Right RR (.Source_1(ALU_Source_1), .Source_2(ALU_Source_2), .out_3(rr_result));
  And AND (.Source_1(ALU_Source_1), .Source_2(ALU_Source_2), .out_3(and_result));
  Inclusive_Or OR (.Source_1(ALU_Source_1), .Source_2(ALU_Source_2), .out_3(or_result));
  Exclusive_Or XOR (.Source_1(ALU_Source_1), .Source_2(ALU_Source_2), .out_3(xor_result));
  Addition ADD (.Source_1(ALU_Source_1), .Source_2(ALU_Source_2), .out_3(add_result));
  Subtraction SUB (.Source_1(ALU_Source_1), .Source_2(ALU_Source_2), .out_3(sub_result));
  ADD1 ADD1 (.Source_1(ALU_Source_1), .Source_2(ALU_Source_2), .out_3(add1_result));
  ADD2 ADD2 (.Source_1(ALU_Source_1), .Source_2(ALU_Source_2), .out_3(add2_result));
  Signed_Comparison SCOMP (.Source_1(ALU_Source_1), .Source_2(ALU_Source_2), .out_3(scomp_result));
  Unsigned_Comparison UCOMP (.Source_1(ALU_Source_1), .Source_2(ALU_Source_2), .out_3(ucomp_result));
  _14 _14th (.Source_1(ALU_Source_1), .Source_2(ALU_Source_2), .out_3(_14_result));
  _15 _15th (.Source_1(ALU_Source_1), .Source_2(ALU_Source_2), .out_3(_15_result));
  Multiplexer #(.select(4), .width(24)) multiplexer_1 (
    .in0(sll_result), .in1(srl_result), .in2(sra_result), .in3(rl_result), .in4(rr_result), .in5(and_result),
    .in6(or_result), .in7(xor_result), .in8(add_result), .in9(sub_result), .in10(add1_result),
    .in11(add2_result), .in12(scomp_result), .in13(ucomp_result), .in14(_14_result), .in15(_15_result),
    .out(ALU_Result), .sel(Operation));  // open: en

  // Other names for the same wires on the sheet: op[3:0] = Operation; result[23:0] = ALU_Result;
  //   s1[23:0] = ALU_Source_1; s2[23:0] = ALU_Source_2

  // Notes on the sheet:
  //   INPUTS
  //   INPUT PROBES
  //   DO NOT MOVE/ADD/CHANGE ANY INPUT OR OUTPUT PINS!
  //   OUTPUT PROBES
  //   OUTPUT
endmodule

module Shift_Left_Logical (
  input  [23:0] in_1,
  input  [23:0] in_2,
  output [23:0] out_3
);

  wire [4:0] bit_extender_1_out;

  Bit_Extender #(.in_width(24), .out_width(5)) bit_extender_1 (.in(in_2), .out(bit_extender_1_out));
  Shifter #(.width(24)) shifter_1 (.in(in_1), .\dist (bit_extender_1_out), .out(out_3));

  // Notes on the sheet:
  //   Source 1
  //   Source 2
endmodule

module Shift_Right_Logical (
  input  [23:0] Source_1,
  input  [23:0] Source_2,
  output [23:0] out_3
);

  wire [4:0] bit_extender_1_out;

  Bit_Extender #(.in_width(24), .out_width(5)) bit_extender_1 (.in(Source_2), .out(bit_extender_1_out));
  Shifter #(.width(24), .shift("lr")) shifter_1 (.in(Source_1), .\dist (bit_extender_1_out), .out(out_3));
endmodule

module Shift_Right_Arithmetic (
  input  [23:0] Source_1,
  input  [23:0] Source_2,
  output [23:0] out_3
);

  wire [4:0] bit_extender_1_out;

  Bit_Extender #(.in_width(24), .out_width(5)) bit_extender_1 (.in(Source_2), .out(bit_extender_1_out));
  Shifter #(.width(24), .shift("ar")) shifter_1 (.in(Source_1), .\dist (bit_extender_1_out), .out(out_3));
endmodule

module Rotate_Left (
  input  [23:0] Source_1,
  input  [23:0] Source_2,
  output [23:0] out_3
);

  wire [4:0] bit_extender_1_out;

  Bit_Extender #(.in_width(24), .out_width(5)) bit_extender_1 (.in(Source_2), .out(bit_extender_1_out));
  Shifter #(.width(24), .shift("rl")) shifter_1 (.in(Source_1), .\dist (bit_extender_1_out), .out(out_3));
endmodule

module Rotate_Right (
  input  [23:0] Source_1,
  input  [23:0] Source_2,
  output [23:0] out_3
);

  wire [4:0] bit_extender_1_out;

  Bit_Extender #(.in_width(24), .out_width(5)) bit_extender_1 (.in(Source_2), .out(bit_extender_1_out));
  Shifter #(.width(24), .shift("rr")) shifter_1 (.in(Source_1), .\dist (bit_extender_1_out), .out(out_3));
endmodule

module And (
  input  [23:0] Source_1,
  input  [23:0] Source_2,
  output [23:0] out_3
);

  assign out_3 = Source_1 & Source_2;  // AND_Gate and_1, 24 bits wide
endmodule

module Inclusive_Or (
  input  [23:0] Source_1,
  input  [23:0] Source_2,
  output [23:0] out_3
);

  assign out_3 = Source_1 | Source_2;  // OR_Gate or_1, 24 bits wide
endmodule

module Exclusive_Or (
  input  [23:0] Source_1,
  input  [23:0] Source_2,
  output [23:0] out_3
);

  wire [23:0] and_1_out, and_2_out, not_1_out, not_2_out;

  assign not_1_out = ~Source_1;  // NOT_Gate not_1, 24 bits wide
  assign and_1_out = not_1_out & Source_2;  // AND_Gate and_1, 24 bits wide
  assign and_2_out = Source_1 & not_2_out;  // AND_Gate and_2, 24 bits wide
  assign not_2_out = ~Source_2;  // NOT_Gate not_2, 24 bits wide
  assign out_3 = and_1_out | and_2_out;  // OR_Gate or_1, 24 bits wide
endmodule

module Addition (
  input  [23:0] Source_1,
  input  [23:0] Source_2,
  output [23:0] out_3
);

  Adder #(.width(24)) adder_1 (.a(Source_1), .b(Source_2), .out(out_3));  // open: cin, cout
endmodule

module Subtraction (
  input  [23:0] Source_1,
  input  [23:0] Source_2,
  output [23:0] out_3
);

  Subtractor #(.width(24)) subtractor_1 (.a(Source_1), .b(Source_2), .out(out_3));  // open: bin, bout
endmodule

module Signed_Comparison (
  input  [23:0] Source_1,
  input  [23:0] Source_2,
  output [23:0] out_3
);

  wire [6:1] or_1_out;

  Comparator #(.width(24)) comparator_1 (
    .a(Source_1), .b(Source_2), .gt(or_1_out[2]), .eq(or_1_out[4]), .lt(or_1_out[6]));
  or or_1 (or_1_out[1], or_1_out[6], or_1_out[4]);
  or or_2 (or_1_out[5], or_1_out[4], or_1_out[2]);
  not not_1 (or_1_out[3], or_1_out[4]);
  assign out_3 = {{16{1'b0}}, {1'b1, or_1_out, 1'b0}};  // Bit_Extender bit_extender_1
endmodule

module Unsigned_Comparison (
  input  [23:0] Source_1,
  input  [23:0] Source_2,
  output [23:0] out_3
);

  wire [6:1] or_1_out;

  Comparator #(.width(24), .mode("unsigned")) comparator_1 (
    .a(Source_1), .b(Source_2), .gt(or_1_out[2]), .eq(or_1_out[4]), .lt(or_1_out[6]));
  or or_1 (or_1_out[1], or_1_out[6], or_1_out[4]);
  or or_2 (or_1_out[5], or_1_out[4], or_1_out[2]);
  not not_1 (or_1_out[3], or_1_out[4]);
  assign out_3 = {{16{1'b0}}, {1'b1, or_1_out, 1'b0}};  // Bit_Extender bit_extender_1
endmodule

module selector (
  input  [23:0] SLL,
  input  [23:0] SRL,
  input  [23:0] SRA,
  input  [23:0] RL,
  input  [23:0] RR,
  input  [23:0] AND,
  input  [23:0] OR,
  input  [23:0] XOR,
  input  [3:0] operation,
  input  [23:0] ADD,
  input  [23:0] SUB,
  input  [23:0] ADD1,
  input  [23:0] ADD2,
  input  [23:0] SCOMP,
  input  [23:0] UCOMP,
  input  [23:0] _14,
  input  [23:0] _15,
  output [23:0] result
);

  wire [23:0] and_1_out, and_2_out, and_3_out, and_4_out, and_5_out, and_6_out, and_7_out, and_8_out,
       and_9_out, and_10_out, and_11_out, and_12_out, and_13_out, and_14_out, and_15_out, and_16_out,
       operation_arithmetic_1__14, operation_arithmetic_1__15, operation_arithmetic_1_add,
       operation_arithmetic_1_add1, operation_arithmetic_1_add2, operation_arithmetic_1_and,
       operation_arithmetic_1_or, operation_arithmetic_1_rl, operation_arithmetic_1_rr,
       operation_arithmetic_1_scomp, operation_arithmetic_1_sll, operation_arithmetic_1_sra,
       operation_arithmetic_1_srl, operation_arithmetic_1_sub, operation_arithmetic_1_ucomp,
       operation_arithmetic_1_xor;

  operation_arithmetic operation_arithmetic_1 (
    .operation(operation), .SLL(operation_arithmetic_1_sll), .SRL(operation_arithmetic_1_srl),
    .SRA(operation_arithmetic_1_sra), .RL(operation_arithmetic_1_rl), .RR(operation_arithmetic_1_rr),
    .AND(operation_arithmetic_1_and), .OR(operation_arithmetic_1_or), .XOR(operation_arithmetic_1_xor),
    .ADD(operation_arithmetic_1_add), .SUB(operation_arithmetic_1_sub), .ADD1(operation_arithmetic_1_add1),
    .ADD2(operation_arithmetic_1_add2), .SCOMP(operation_arithmetic_1_scomp),
    .UCOMP(operation_arithmetic_1_ucomp), ._14(operation_arithmetic_1__14), ._15(operation_arithmetic_1__15));
  assign and_1_out = SLL & operation_arithmetic_1_sll;  // AND_Gate and_1, 24 bits wide
  assign and_2_out = SRL & operation_arithmetic_1_srl;  // AND_Gate and_2, 24 bits wide
  assign and_3_out = operation_arithmetic_1__14 & _14;  // AND_Gate and_3, 24 bits wide
  assign and_4_out = operation_arithmetic_1__15 & _15;  // AND_Gate and_4, 24 bits wide
  assign and_5_out = SRA & operation_arithmetic_1_sra;  // AND_Gate and_5, 24 bits wide
  assign and_6_out = RL & operation_arithmetic_1_rl;  // AND_Gate and_6, 24 bits wide
  assign and_7_out = RR & operation_arithmetic_1_rr;  // AND_Gate and_7, 24 bits wide
  assign and_8_out = AND & operation_arithmetic_1_and;  // AND_Gate and_8, 24 bits wide
  assign and_9_out = OR & operation_arithmetic_1_or;  // AND_Gate and_9, 24 bits wide
  assign and_10_out = XOR & operation_arithmetic_1_xor;  // AND_Gate and_10, 24 bits wide
  assign and_11_out = operation_arithmetic_1_add & ADD;  // AND_Gate and_11, 24 bits wide
  assign and_12_out = operation_arithmetic_1_sub & SUB;  // AND_Gate and_12, 24 bits wide
  assign and_13_out = operation_arithmetic_1_add1 & ADD1;  // AND_Gate and_13, 24 bits wide
  assign and_14_out = operation_arithmetic_1_add2 & ADD2;  // AND_Gate and_14, 24 bits wide
  assign and_15_out = operation_arithmetic_1_scomp & SCOMP;  // AND_Gate and_15, 24 bits wide
  assign and_16_out = operation_arithmetic_1_ucomp & UCOMP;  // AND_Gate and_16, 24 bits wide
  assign result = and_1_out | and_2_out | and_5_out | and_6_out | and_7_out | and_8_out | and_9_out | and_10_out | and_11_out | and_12_out | and_13_out | and_14_out | and_15_out | and_16_out | and_3_out | and_4_out;  // OR_Gate or_1, 24 bits wide
endmodule

module sel_SLL (
  input  [3:0] operation,
  output out_2
);

  wire not_1_out, not_2_out, not_3_out, not_4_out, operation_split_1_lsb, operation_split_1_msb,
       operation_split_1_out_3, operation_split_1_out_4;

  operation_split operation_split_1 (
    .Operation(operation), .LSB(operation_split_1_lsb), .out_3(operation_split_1_out_3),
    .out_4(operation_split_1_out_4), .MSB(operation_split_1_msb));
  not not_1 (not_1_out, operation_split_1_lsb);
  not not_2 (not_2_out, operation_split_1_out_3);
  not not_3 (not_3_out, operation_split_1_out_4);
  not not_4 (not_4_out, operation_split_1_msb);
  and and_1 (out_2, not_1_out, not_2_out, not_3_out, not_4_out);
endmodule

module sel_SRL (
  input  [3:0] operation,
  output out_2
);

  wire not_1_out, not_2_out, not_3_out, operation_split_1_lsb, operation_split_1_msb,
       operation_split_1_out_3, operation_split_1_out_4;

  operation_split operation_split_1 (
    .Operation(operation), .LSB(operation_split_1_lsb), .out_3(operation_split_1_out_3),
    .out_4(operation_split_1_out_4), .MSB(operation_split_1_msb));
  not not_1 (not_1_out, operation_split_1_out_3);
  not not_2 (not_2_out, operation_split_1_out_4);
  not not_3 (not_3_out, operation_split_1_msb);
  and and_1 (out_2, operation_split_1_lsb, not_1_out, not_2_out, not_3_out);
endmodule

module sel_SRA (
  input  [3:0] operation,
  output out_2
);

  wire not_1_out, not_2_out, operation_split_1_lsb, operation_split_1_msb, operation_split_1_out_3,
       operation_split_1_out_4;

  operation_split operation_split_1 (
    .Operation(operation), .LSB(operation_split_1_lsb), .out_3(operation_split_1_out_3),
    .out_4(operation_split_1_out_4), .MSB(operation_split_1_msb));
  not not_1 (not_1_out, operation_split_1_out_4);
  not not_2 (not_2_out, operation_split_1_msb);
  and and_1 (out_2, operation_split_1_lsb, operation_split_1_out_3, not_1_out, not_2_out);
endmodule

module sel_RL (
  input  [3:0] operation,
  output out_2
);

  wire not_1_out, not_2_out, not_3_out, operation_split_1_lsb, operation_split_1_msb,
       operation_split_1_out_3, operation_split_1_out_4;

  operation_split operation_split_1 (
    .Operation(operation), .LSB(operation_split_1_lsb), .out_3(operation_split_1_out_3),
    .out_4(operation_split_1_out_4), .MSB(operation_split_1_msb));
  not not_1 (not_1_out, operation_split_1_lsb);
  not not_2 (not_2_out, operation_split_1_out_3);
  not not_3 (not_3_out, operation_split_1_msb);
  and and_1 (out_2, not_1_out, not_2_out, operation_split_1_out_4, not_3_out);
endmodule

module sel_RR (
  input  [3:0] operation,
  output out_2
);

  wire not_1_out, not_2_out, operation_split_1_lsb, operation_split_1_msb, operation_split_1_out_3,
       operation_split_1_out_4;

  operation_split operation_split_1 (
    .Operation(operation), .LSB(operation_split_1_lsb), .out_3(operation_split_1_out_3),
    .out_4(operation_split_1_out_4), .MSB(operation_split_1_msb));
  not not_1 (not_1_out, operation_split_1_out_3);
  not not_2 (not_2_out, operation_split_1_msb);
  and and_1 (out_2, operation_split_1_lsb, not_1_out, operation_split_1_out_4, not_2_out);
endmodule

module sel_AND (
  input  [3:0] operation,
  output out_2
);

  wire not_1_out, not_2_out, operation_split_1_lsb, operation_split_1_msb, operation_split_1_out_3,
       operation_split_1_out_4;

  operation_split operation_split_1 (
    .Operation(operation), .LSB(operation_split_1_lsb), .out_3(operation_split_1_out_3),
    .out_4(operation_split_1_out_4), .MSB(operation_split_1_msb));
  not not_1 (not_1_out, operation_split_1_out_3);
  not not_2 (not_2_out, operation_split_1_msb);
  and and_1 (out_2, operation_split_1_lsb, not_1_out, operation_split_1_out_4, not_2_out);
endmodule

module sel_OR (
  input  [3:0] operation,
  output out_2
);

  wire not_1_out, not_2_out, operation_split_1_lsb, operation_split_1_msb, operation_split_1_out_3,
       operation_split_1_out_4;

  operation_split operation_split_1 (
    .Operation(operation), .LSB(operation_split_1_lsb), .out_3(operation_split_1_out_3),
    .out_4(operation_split_1_out_4), .MSB(operation_split_1_msb));
  not not_1 (not_1_out, operation_split_1_lsb);
  not not_2 (not_2_out, operation_split_1_msb);
  and and_1 (out_2, not_1_out, operation_split_1_out_3, operation_split_1_out_4, not_2_out);
endmodule

module sel_XOR (
  input  [3:0] operation,
  output out_2
);

  wire not_1_out, operation_split_1_lsb, operation_split_1_msb, operation_split_1_out_3,
       operation_split_1_out_4;

  operation_split operation_split_1 (
    .Operation(operation), .LSB(operation_split_1_lsb), .out_3(operation_split_1_out_3),
    .out_4(operation_split_1_out_4), .MSB(operation_split_1_msb));
  not not_1 (not_1_out, operation_split_1_msb);
  and and_1 (out_2, operation_split_1_lsb, operation_split_1_out_3, operation_split_1_out_4, not_1_out);
endmodule

module sel_ADD (
  input  [3:0] operation,
  output out_2
);

  wire not_1_out, not_2_out, not_3_out, operation_split_1_lsb, operation_split_1_msb,
       operation_split_1_out_3, operation_split_1_out_4;

  operation_split operation_split_1 (
    .Operation(operation), .LSB(operation_split_1_lsb), .out_3(operation_split_1_out_3),
    .out_4(operation_split_1_out_4), .MSB(operation_split_1_msb));
  not not_1 (not_1_out, operation_split_1_lsb);
  not not_2 (not_2_out, operation_split_1_out_3);
  not not_3 (not_3_out, operation_split_1_out_4);
  and and_1 (out_2, not_1_out, not_2_out, not_3_out, operation_split_1_msb);
endmodule

module sel_SUB (
  input  [3:0] operation,
  output out_2
);

  wire not_1_out, not_2_out, operation_split_1_lsb, operation_split_1_msb, operation_split_1_out_3,
       operation_split_1_out_4;

  operation_split operation_split_1 (
    .Operation(operation), .LSB(operation_split_1_lsb), .out_3(operation_split_1_out_3),
    .out_4(operation_split_1_out_4), .MSB(operation_split_1_msb));
  not not_1 (not_1_out, operation_split_1_out_3);
  not not_2 (not_2_out, operation_split_1_out_4);
  and and_1 (out_2, operation_split_1_lsb, not_1_out, not_2_out, operation_split_1_msb);
endmodule

module sel_SCOMP (
  input  [3:0] operation,
  output out_2
);

  wire not_1_out, not_2_out, operation_split_1_lsb, operation_split_1_msb, operation_split_1_out_3,
       operation_split_1_out_4;

  operation_split operation_split_1 (
    .Operation(operation), .LSB(operation_split_1_lsb), .out_3(operation_split_1_out_3),
    .out_4(operation_split_1_out_4), .MSB(operation_split_1_msb));
  not not_1 (not_1_out, operation_split_1_lsb);
  not not_2 (not_2_out, operation_split_1_out_3);
  and and_1 (out_2, not_1_out, not_2_out, operation_split_1_out_4, operation_split_1_msb);
endmodule

module sel_UCOMP (
  input  [3:0] operation,
  output out_2
);

  wire not_1_out, operation_split_1_lsb, operation_split_1_msb, operation_split_1_out_3,
       operation_split_1_out_4;

  operation_split operation_split_1 (
    .Operation(operation), .LSB(operation_split_1_lsb), .out_3(operation_split_1_out_3),
    .out_4(operation_split_1_out_4), .MSB(operation_split_1_msb));
  not not_1 (not_1_out, operation_split_1_out_3);
  and and_1 (out_2, operation_split_1_lsb, not_1_out, operation_split_1_out_4, operation_split_1_msb);
endmodule

module operation_split (
  input  [3:0] Operation,
  output LSB,
  output out_3,
  output out_4,
  output MSB
);


  assign LSB = Operation[0];
  assign MSB = Operation[3];
  assign out_3 = Operation[1];
  assign out_4 = Operation[2];
endmodule

module sel_ADD1 (
  input  [3:0] operation,
  output out_2
);

  wire not_1_out, not_2_out, operation_split_1_lsb, operation_split_1_msb, operation_split_1_out_3,
       operation_split_1_out_4;

  operation_split operation_split_1 (
    .Operation(operation), .LSB(operation_split_1_lsb), .out_3(operation_split_1_out_3),
    .out_4(operation_split_1_out_4), .MSB(operation_split_1_msb));
  not not_1 (not_1_out, operation_split_1_lsb);
  not not_2 (not_2_out, operation_split_1_out_4);
  and and_1 (out_2, not_1_out, operation_split_1_out_3, not_2_out, operation_split_1_msb);
endmodule

module sel_ADD2 (
  input  [3:0] operation,
  output out_2
);

  wire not_1_out, operation_split_1_lsb, operation_split_1_msb, operation_split_1_out_3,
       operation_split_1_out_4;

  operation_split operation_split_1 (
    .Operation(operation), .LSB(operation_split_1_lsb), .out_3(operation_split_1_out_3),
    .out_4(operation_split_1_out_4), .MSB(operation_split_1_msb));
  not not_1 (not_1_out, operation_split_1_out_4);
  and and_1 (out_2, operation_split_1_lsb, operation_split_1_out_3, not_1_out, operation_split_1_msb);
endmodule

module ADD1 (
  input  [23:0] Source_1,
  input  [23:0] Source_2,
  output [23:0] out_3
);

  Adder #(.width(24)) adder_1 (.a(Source_1), .b(Source_2), .out(out_3));  // open: cin, cout
endmodule

module ADD2 (
  input  [23:0] Source_1,
  input  [23:0] Source_2,
  output [23:0] out_3
);

  Adder #(.width(24)) adder_1 (.a(Source_1), .b(Source_2), .out(out_3));  // open: cin, cout
endmodule

module _14 (
  input  [23:0] Source_1,
  input  [23:0] Source_2,
  output [23:0] out_3
);

  wire [23:0] adder_1_out;

  Adder #(.width(24)) adder_1 (.a(Source_1), .b(Source_2), .out(adder_1_out));  // open: cin, cout
  assign out_3 = adder_1_out & {24{1'b0}};  // AND_Gate and_1, 24 bits wide
endmodule

module _15 (
  input  [23:0] Source_1,
  input  [23:0] Source_2,
  output [23:0] out_3
);

  wire [23:0] adder_1_out;

  Adder #(.width(24)) adder_1 (.a(Source_1), .b(Source_2), .out(adder_1_out));  // open: cin, cout
  assign out_3 = adder_1_out & {24{1'b0}};  // AND_Gate and_1, 24 bits wide
endmodule

module operation_arithmetic (
  input  [3:0] operation,
  output [23:0] SLL,
  output [23:0] SRL,
  output [23:0] SRA,
  output [23:0] RL,
  output [23:0] RR,
  output [23:0] AND,
  output [23:0] OR,
  output [23:0] XOR,
  output [23:0] ADD,
  output [23:0] SUB,
  output [23:0] ADD1,
  output [23:0] ADD2,
  output [23:0] SCOMP,
  output [23:0] UCOMP,
  output [23:0] _14,
  output [23:0] _15
);

  wire sel_14_out_2, sel_15_out_2, sel_ADD1_out_2, sel_ADD2_out_2, sel_ADD_out_2, sel_AND_out_2,
       sel_OR_out_2, sel_RL_out_2, sel_RR_out_2, sel_SCOMP_out_2, sel_SLL_out_2, sel_SRA_out_2,
       sel_SRL_out_2, sel_SUB_out_2, sel_UCOMP_out_2, sel_XOR_out_2;

  sel_SLL sel_SLL (.operation(operation), .out_2(sel_SLL_out_2));
  sel_SRL sel_SRL (.operation(operation), .out_2(sel_SRL_out_2));
  sel_SRA sel_SRA (.operation(operation), .out_2(sel_SRA_out_2));
  sel_RL sel_RL (.operation(operation), .out_2(sel_RL_out_2));
  sel_RR sel_RR (.operation(operation), .out_2(sel_RR_out_2));
  sel_AND sel_AND (.operation(operation), .out_2(sel_AND_out_2));
  sel_OR sel_OR (.operation(operation), .out_2(sel_OR_out_2));
  sel_XOR sel_XOR (.operation(operation), .out_2(sel_XOR_out_2));
  sel_ADD sel_ADD (.operation(operation), .out_2(sel_ADD_out_2));
  sel_SUB sel_SUB (.operation(operation), .out_2(sel_SUB_out_2));
  sel_ADD1 sel_ADD1 (.operation(operation), .out_2(sel_ADD1_out_2));
  sel_ADD2 sel_ADD2 (.operation(operation), .out_2(sel_ADD2_out_2));
  sel_SCOMP sel_SCOMP (.operation(operation), .out_2(sel_SCOMP_out_2));
  sel_UCOMP sel_UCOMP (.operation(operation), .out_2(sel_UCOMP_out_2));
  sel_14 sel_14 (.operation(operation), .out_2(sel_14_out_2));
  sel_15 sel_15 (.operation(operation), .out_2(sel_15_out_2));
  assign SLL = {{23{sel_SLL_out_2}}, sel_SLL_out_2};  // Bit_Extender bit_extender_1
  assign SRA = {{23{sel_SRA_out_2}}, sel_SRA_out_2};  // Bit_Extender bit_extender_2
  assign RR = {{23{sel_RR_out_2}}, sel_RR_out_2};  // Bit_Extender bit_extender_3
  assign OR = {{23{sel_OR_out_2}}, sel_OR_out_2};  // Bit_Extender bit_extender_4
  assign ADD = {{23{sel_ADD_out_2}}, sel_ADD_out_2};  // Bit_Extender bit_extender_5
  assign ADD1 = {{23{sel_ADD1_out_2}}, sel_ADD1_out_2};  // Bit_Extender bit_extender_6
  assign SCOMP = {{23{sel_SCOMP_out_2}}, sel_SCOMP_out_2};  // Bit_Extender bit_extender_7
  assign _14 = {{23{sel_14_out_2}}, sel_14_out_2};  // Bit_Extender bit_extender_8
  assign SRL = {{23{sel_SRL_out_2}}, sel_SRL_out_2};  // Bit_Extender bit_extender_9
  assign RL = {{23{sel_RL_out_2}}, sel_RL_out_2};  // Bit_Extender bit_extender_10
  assign AND = {{23{sel_AND_out_2}}, sel_AND_out_2};  // Bit_Extender bit_extender_11
  assign XOR = {{23{sel_XOR_out_2}}, sel_XOR_out_2};  // Bit_Extender bit_extender_12
  assign SUB = {{23{sel_SUB_out_2}}, sel_SUB_out_2};  // Bit_Extender bit_extender_13
  assign ADD2 = {{23{sel_ADD2_out_2}}, sel_ADD2_out_2};  // Bit_Extender bit_extender_14
  assign UCOMP = {{23{sel_UCOMP_out_2}}, sel_UCOMP_out_2};  // Bit_Extender bit_extender_15
  assign _15 = {{23{sel_15_out_2}}, sel_15_out_2};  // Bit_Extender bit_extender_16
endmodule

module sel_14 (
  input  [3:0] operation,
  output out_2
);

  wire not_1_out, operation_split_1_lsb, operation_split_1_msb, operation_split_1_out_3,
       operation_split_1_out_4;

  operation_split operation_split_1 (
    .Operation(operation), .LSB(operation_split_1_lsb), .out_3(operation_split_1_out_3),
    .out_4(operation_split_1_out_4), .MSB(operation_split_1_msb));
  not not_1 (not_1_out, operation_split_1_lsb);
  and and_1 (out_2, not_1_out, operation_split_1_out_3, operation_split_1_out_4, operation_split_1_msb);
endmodule

module sel_15 (
  input  [3:0] operation,
  output out_2
);

  wire not_1_out, not_2_out, operation_split_1_lsb, operation_split_1_msb, operation_split_1_out_3,
       operation_split_1_out_4;

  operation_split operation_split_1 (
    .Operation(operation), .LSB(operation_split_1_lsb), .out_3(operation_split_1_out_3),
    .out_4(operation_split_1_out_4), .MSB(operation_split_1_msb));
  not not_1 (not_1_out, operation_split_1_out_3);
  not not_2 (not_2_out, operation_split_1_out_4);
  and and_1 (out_2, operation_split_1_lsb, not_1_out, not_2_out, operation_split_1_msb);
endmodule
