// Logisim project CPU.circ as structural Verilog: 7 circuits, main circuit Ida CPU
// CPU
module Ida_CPU (
  input  [31:0] Instruction,
  input  Clock,
  output [23:0] Mem_Data,
  output [23:0] Mem_Address,
  output Mem_Write,
  output [23:0] Next_PC,
  output [23:0] r00,
  output [23:0] r01,
  output [23:0] r02,
  output [23:0] r03,
  output [23:0] r04,
  output [23:0] r05,
  output [23:0] r06,
  output [23:0] r07,
  output [23:0] r08,
  output [23:0] r09,
  output [23:0] r10,
  output [23:0] r11,
  output [23:0] r12,
  output [23:0] r13,
  output [23:0] r14,
  output [23:0] r15
);

  wire _12, _13, _14, _15, A1, A2, bitselector_1_out, bitselector_2_out, bitselector_3_out,
       bitselector_4_out, bitselector_5_out, bitselector_6_out, bitselector_7_out, bitselector_8_out,
       bitselector_9_out, bitselector_10_out, bitselector_11_out, bitselector_12_out, bitselector_13_out,
       bitselector_14_out, bitselector_15_out, bitselector_16_out, comp, imm_t, jump, link, load, not_1_out,
       not_2_out, not_3_out, not_4_out, reg_write, register_2_q, True;
  wire [2:0] CQ;
  wire [3:0] opcode, RD, RI, RS, write_reg;
  wire [7:0] CQ_t, or_3_out;
  wire [23:0] adder_logic_1_next_pc, bit_extender_1_out, cr_q, imm, load_data, multiplexer_1_out,
       multiplexer_3_out, multiplexer_4_out, multiplexer_5_out, multiplexer_8_out, nxtinst, reg1_val,
       reg2_val, sel_reg1_val, sel_reg2_val, write_val;
  wire [31:0] multiplexer_2_out, register_1_q;

  // Probe on Instruction
  // Probe on Clock
  // Probe on r00
  // Probe on r01
  // Probe on r02
  // Probe on r03
  // Probe on r04
  // Probe on r05
  // Probe on r06
  // Probe on r07
  // Probe on Mem_Data
  // Probe on Mem_Address
  // Probe on Mem_Write
  // Probe on Next_PC
  // Probe on r08
  // Probe on r09
  // Probe on r10
  // Probe on r11
  // Probe on r12
  // Probe on r13
  // Probe on r14
  // Probe on r15
  or or_1 (A2, _12, _13);
  or or_2 (A1, _14, _15);
  BitSelector #(.width(4)) bitselector_1 (.in(opcode), .out(bitselector_1_out), .sel(2'b11));
  BitSelector #(.width(4)) bitselector_2 (.in(opcode), .out(bitselector_2_out), .sel(2'b10));
  BitSelector #(.width(4)) bitselector_3 (.in(opcode), .out(bitselector_3_out), .sel(2'b01));
  BitSelector #(.width(4)) bitselector_4 (.in(opcode), .out(bitselector_4_out), .sel(2'b00));
  BitSelector #(.width(4)) bitselector_5 (.in(opcode), .out(bitselector_5_out), .sel(2'b11));
  BitSelector #(.width(4)) bitselector_6 (.in(opcode), .out(bitselector_6_out), .sel(2'b10));
  BitSelector #(.width(4)) bitselector_7 (.in(opcode), .out(bitselector_7_out), .sel(2'b01));
  BitSelector #(.width(4)) bitselector_8 (.in(opcode), .out(bitselector_8_out), .sel(2'b00));
  BitSelector #(.width(4)) bitselector_9 (.in(opcode), .out(bitselector_9_out), .sel(2'b11));
  BitSelector #(.width(4)) bitselector_10 (.in(opcode), .out(bitselector_10_out), .sel(2'b10));
  BitSelector #(.width(4)) bitselector_11 (.in(opcode), .out(bitselector_11_out), .sel(2'b01));
  BitSelector #(.width(4)) bitselector_12 (.in(opcode), .out(bitselector_12_out), .sel(2'b00));
  BitSelector #(.width(4)) bitselector_13 (.in(opcode), .out(bitselector_13_out), .sel(2'b11));
  BitSelector #(.width(4)) bitselector_14 (.in(opcode), .out(bitselector_14_out), .sel(2'b10));
  BitSelector #(.width(4)) bitselector_15 (.in(opcode), .out(bitselector_15_out), .sel(2'b01));
  BitSelector #(.width(4)) bitselector_16 (.in(opcode), .out(bitselector_16_out), .sel(2'b00));
  and and_1 (_12, bitselector_1_out, bitselector_2_out, not_1_out, not_2_out);
  not not_1 (not_1_out, bitselector_3_out);
  not not_2 (not_2_out, bitselector_4_out);
  and and_2 (_13, bitselector_5_out, bitselector_6_out, not_3_out, bitselector_8_out);
  not not_3 (not_3_out, bitselector_7_out);
  and and_3 (_14, bitselector_9_out, bitselector_10_out, bitselector_11_out, not_4_out);
  not not_4 (not_4_out, bitselector_12_out);
  and and_4 (_15, bitselector_13_out, bitselector_14_out, bitselector_15_out, bitselector_16_out);
  // Probe on RD
  // Probe on RS
  // Probe on RI
  // Probe on imm
  // Probe on CQ_t
  // Probe on A2
  // Probe on A1
  Multiplexer #(.width(24)) multiplexer_1 (
    .in0(reg2_val), .in1(imm), .out(multiplexer_1_out), .sel(imm_t));  // open: en
  Adder_Logic adder_logic_1 (
    .pc(Next_PC), .sel_imm(multiplexer_1_out), .opcode(opcode), .next_pc(adder_logic_1_next_pc));
  assign or_3_out = CQ_t | 8'h80;  // OR_Gate or_3, 8 bits wide
  Register #(.width(32)) register_1 (.D(Instruction), .Q(register_1_q), .clk(Clock));  // open: en, clr
  Register #(.width(1)) register_2 (.D(jump), .Q(register_2_q), .clk(Clock));  // open: en, clr
  Register #(.width(24)) PC (.D(adder_logic_1_next_pc), .Q(Next_PC), .clk(Clock));  // open: en, clr
  Multiplexer #(.width(32)) multiplexer_2 (
    .in0(register_1_q), .in1({32{1'b0}}), .out(multiplexer_2_out), .sel(register_2_q));  // open: en
  assign bit_extender_1_out = {{16{1'b0}}, or_3_out};  // Bit_Extender bit_extender_1
  Multiplexer #(.width(24)) multiplexer_3 (
    .in0(bit_extender_1_out), .in1(Mem_Address), .out(multiplexer_3_out), .sel(comp));  // open: en
  decoder decoder_1 (.inst(multiplexer_2_out), .opcode(opcode), .CQ(CQ), .Imm(imm_t), .nxtInst(nxtinst));
  BitSelector bitselector_17 (.in(or_3_out), .out(True), .sel(CQ));
  Register #(.width(24)) cr (.D(multiplexer_3_out), .Q(cr_q), .clk(Clock));  // open: en, clr
  Multiplexer #(.width(24)) multiplexer_4 (
    .in0(Mem_Address), .in1(load_data), .out(multiplexer_4_out), .sel(load));  // open: en
  Multiplexer #(.width(24)) multiplexer_5 (
    .in0(reg2_val), .in1(imm), .out(multiplexer_5_out), .sel(imm_t));  // open: en
  Multiplexer #(.width(4)) multiplexer_6 (.in0(RD), .in1(4'b0010), .out(write_reg), .sel(link));  // open: en
  Bit_Extender #(.in_width(24), .out_width(8)) bit_extender_2 (.in(cr_q), .out(CQ_t));
  select_instruction select_instruction_1 (
    .imm(imm_t), .CQ(True), .opcode(opcode), .next_inst(nxtinst), .RD(RD), .RS(RS), .RI(RI), .Immediate(imm));
  Multiplexer #(.width(24)) multiplexer_7 (
    .in0(multiplexer_4_out), .in1(multiplexer_5_out), .out(write_val), .sel(link));  // open: en
  Ida_Register_File ida_register_file_1 (
    .Read_Reg_1(RS), .Read_Reg_2(RI), .Write_Reg(write_reg), .Write_Value(write_val), .Reg_1_Value(reg1_val),
    .Reg_2_Value(reg2_val), .Reg_Write(reg_write), .Clock(Clock), .r00(r00), .r01(r01), .r02(r02), .r03(r03),
    .r04(r04), .r05(r05), .r06(r06), .r07(r07), .r08(r08), .r09(r09), .r10(r10), .r11(r11), .r12(r12),
    .r13(r13), .r14(r14), .r15(r15), .Reg_3_Value(Mem_Data));
  control control_1 (
    .opcode(opcode), .jump(jump), .link(link), .reg_write(reg_write), .memWrite(Mem_Write), .load(load),
    .comp(comp));
  Ida_ALU ida_alu_1 (
    .ALU_Source_1(sel_reg1_val), .ALU_Source_2(sel_reg2_val), .Operation(opcode), .ALU_Result(Mem_Address));
  Multiplexer #(.width(24)) multiplexer_8 (
    .in0(reg2_val), .in1(imm), .out(multiplexer_8_out), .sel(imm_t));  // open: en
  RAM #(.addrWidth(24), .dataWidth(24), .bus("separate")) ram_1 (
    .addr(Mem_Address), .din(Mem_Data), .data(load_data), .str(Mem_Write), .clk(Clock), .ld(load));  // open: sel, clr
  Multiplexer #(.width(24)) multiplexer_9 (
    .in0(multiplexer_8_out), .in1({24{1'b0}}), .out(sel_reg2_val), .sel(jump));  // open: en
  Multiplexer #(.width(24)) multiplexer_10 (
    .in0(reg1_val), .in1(Mem_Data), .out(sel_reg1_val), .sel(comp));  // open: en

  // Other names for the same wires on the sheet: clk = Clock; inst[31:0] = Instruction; memWrite = Mem_Write;
  //   nextPC[23:0] = Next_PC; memData[23:0] = Mem_Data; reg3_val[23:0] = Mem_Data; memAddr[23:0] = Mem_Address;
  //   result[23:0] = Mem_Address

  // Notes on the sheet:
  //   INPUTS
  //   INPUT PROBES
  //   OUTPUT PROBES
  //   constants
  //   A2/A3 switches
  //   instruction selectors
  //   12th instruction selector
  //   13th instruction selector
  //   14th instruction selector
  //   15th instruction selector
  //   OUTPUTS
  //   DO NOT MOVE/ADD/CHANGE ANY INPUT OR OUTPUT PINS!
  //   PC control
  //   make sure ?OK is set to 1
  //   CR control
  //   select comparison request
  //   if comp, store into %cr
  //   decode
  //   sel write val
  //   sel write reg
  //   if link inst, select reg2
  //   REG Circ
  //   Control
  //   ALU Circ
  //   sel reg2
  //   select register or immediate
  //   Memory
  //   if jump, nop
  //   sel reg1
endmodule

module no_IMM_inst (
  input  [23:0] other,
  output [3:0] A3__RD,
  output [3:0] A3__RS,
  output [3:0] A3__RI,
  output [3:0] A2__RD,
  output [3:0] A2__RI,
  output [3:0] A1__RI
);


  assign A1__RI = other[3:0];
  assign A2__RD = other[23:20];
  assign A2__RI = other[3:0];
  assign A3__RD = other[23:20];
  assign A3__RI = other[3:0];
  assign A3__RS = other[19:16];

  // Notes on the sheet:
  //   A3 type
  //   A2 type
  //   A1 type
endmodule

module IMM_inst (
  input  _13th_inst,
  input  [23:0] other,
  output [3:0] A3__RD,
  output [3:0] A3__RS,
  output [23:0] A3__RI,
  output [3:0] A2__RD,
  output [23:0] A2__RI,
  output [23:0] A1__RI
);

  wire [23:0] bit_extender_1_out, bit_extender_2_out, bit_extender_3_out, bit_extender_4_out;

  assign bit_extender_1_out = {{8{other[15]}}, other[15:0]};  // Bit_Extender bit_extender_1
  assign bit_extender_2_out = {{8{1'b0}}, other[15:0]};  // Bit_Extender bit_extender_2
  assign bit_extender_3_out = {{4{other[19]}}, other[19:0]};  // Bit_Extender bit_extender_3
  assign bit_extender_4_out = {{4{1'b0}}, other[19:0]};  // Bit_Extender bit_extender_4
  Multiplexer #(.width(24)) multiplexer_1 (
    .in0(bit_extender_1_out), .in1(bit_extender_2_out), .out(A3__RI), .sel(_13th_inst));  // open: en
  Multiplexer #(.width(24)) multiplexer_2 (
    .in0(bit_extender_3_out), .in1(bit_extender_4_out), .out(A2__RI), .sel(_13th_inst));  // open: en

  assign A1__RI = other;
  assign A2__RD = other[23:20];
  assign A3__RD = other[23:20];
  assign A3__RS = other[19:16];

  // Notes on the sheet:
  //   A3 type
  //   A2 type
  //   A1 type
endmodule

module select_instruction (
  input  imm,
  input  CQ,
  input  [3:0] opcode,
  input  [23:0] next_inst,
  output [3:0] RD,
  output [3:0] RS,
  output [3:0] RI,
  output [23:0] Immediate
);

  wire _12, _13, _14, _15, A1, A2, bitselector_1_out, bitselector_2_out, bitselector_3_out,
       bitselector_4_out, bitselector_5_out, bitselector_6_out, bitselector_7_out, bitselector_8_out,
       bitselector_9_out, bitselector_10_out, bitselector_11_out, bitselector_12_out, bitselector_13_out,
       bitselector_14_out, bitselector_15_out, bitselector_16_out, not_1_out, not_2_out, not_3_out, not_4_out;
  wire [3:0] A1__RI, A2__RD, A2__RI, A3__RD, A3__RI, A3__RS, iA2__RD, iA3__RD, iA3__RS, multiplexer_1_out,
       multiplexer_2_out, multiplexer_4_out, multiplexer_5_out, multiplexer_6_out, multiplexer_7_out,
       multiplexer_8_out, multiplexer_10_out, multiplexer_13_out;
  wire [23:0] iA1_imm, iA2_imm, iA3_imm, multiplexer_3_out, multiplexer_9_out, multiplexer_14_out;

  BitSelector #(.width(4)) bitselector_1 (.in(opcode), .out(bitselector_1_out), .sel(2'b11));
  BitSelector #(.width(4)) bitselector_2 (.in(opcode), .out(bitselector_2_out), .sel(2'b10));
  not not_1 (not_1_out, bitselector_3_out);
  BitSelector #(.width(4)) bitselector_3 (.in(opcode), .out(bitselector_3_out), .sel(2'b01));
  not not_2 (not_2_out, bitselector_4_out);
  BitSelector #(.width(4)) bitselector_4 (.in(opcode), .out(bitselector_4_out), .sel(2'b00));
  BitSelector #(.width(4)) bitselector_5 (.in(opcode), .out(bitselector_5_out), .sel(2'b11));
  BitSelector #(.width(4)) bitselector_6 (.in(opcode), .out(bitselector_6_out), .sel(2'b10));
  not not_3 (not_3_out, bitselector_7_out);
  BitSelector #(.width(4)) bitselector_7 (.in(opcode), .out(bitselector_7_out), .sel(2'b01));
  BitSelector #(.width(4)) bitselector_8 (.in(opcode), .out(bitselector_8_out), .sel(2'b00));
  BitSelector #(.width(4)) bitselector_9 (.in(opcode), .out(bitselector_9_out), .sel(2'b11));
  BitSelector #(.width(4)) bitselector_10 (.in(opcode), .out(bitselector_10_out), .sel(2'b10));
  BitSelector #(.width(4)) bitselector_11 (.in(opcode), .out(bitselector_11_out), .sel(2'b01));
  not not_4 (not_4_out, bitselector_12_out);
  BitSelector #(.width(4)) bitselector_12 (.in(opcode), .out(bitselector_12_out), .sel(2'b00));
  BitSelector #(.width(4)) bitselector_13 (.in(opcode), .out(bitselector_13_out), .sel(2'b11));
  BitSelector #(.width(4)) bitselector_14 (.in(opcode), .out(bitselector_14_out), .sel(2'b10));
  BitSelector #(.width(4)) bitselector_15 (.in(opcode), .out(bitselector_15_out), .sel(2'b01));
  BitSelector #(.width(4)) bitselector_16 (.in(opcode), .out(bitselector_16_out), .sel(2'b00));
  and and_1 (_12, bitselector_1_out, bitselector_2_out, not_1_out, not_2_out);
  and and_2 (_13, bitselector_5_out, bitselector_6_out, not_3_out, bitselector_8_out);
  and and_3 (_14, bitselector_9_out, bitselector_10_out, bitselector_11_out, not_4_out);
  and and_4 (_15, bitselector_13_out, bitselector_14_out, bitselector_15_out, bitselector_16_out);
  no_IMM_inst no_imm_inst_1 (
    .other(next_inst), .A3__RD(A3__RD), .A3__RS(A3__RS), .A3__RI(A3__RI), .A2__RD(A2__RD), .A2__RI(A2__RI),
    .A1__RI(A1__RI));
  IMM_inst imm_inst_1 (
    ._13th_inst(_13), .other(next_inst), .A3__RD(iA3__RD), .A3__RS(iA3__RS), .A3__RI(iA3_imm),
    .A2__RD(iA2__RD), .A2__RI(iA2_imm), .A1__RI(iA1_imm));
  or or_1 (A2, _12, _13);
  or or_2 (A1, _14, _15);
  Multiplexer #(.width(4)) multiplexer_1 (.in0(A3__RS), .in1(iA3__RS), .out(multiplexer_1_out), .sel(imm));  // open: en
  Multiplexer #(.width(4)) multiplexer_2 (.in0(A3__RI), .in1(A2__RI), .out(multiplexer_2_out), .sel(A2));  // open: en
  Multiplexer #(.width(24)) multiplexer_3 (
    .in0(iA3_imm), .in1(iA2_imm), .out(multiplexer_3_out), .sel(A2));  // open: en
  Multiplexer #(.width(4)) multiplexer_4 (.in0(A3__RD), .in1(iA3__RD), .out(multiplexer_4_out), .sel(imm));  // open: en
  Multiplexer #(.width(4)) multiplexer_5 (
    .in0(multiplexer_4_out), .in1(multiplexer_6_out), .out(multiplexer_5_out), .sel(A2));  // open: en
  Multiplexer #(.width(4)) multiplexer_6 (.in0(A2__RD), .in1(iA2__RD), .out(multiplexer_6_out), .sel(imm));  // open: en
  Multiplexer #(.width(4)) multiplexer_7 (
    .in0(multiplexer_1_out), .in1(4'b0000), .out(multiplexer_7_out), .sel(A1));  // open: en
  Multiplexer #(.width(4)) multiplexer_8 (
    .in0(multiplexer_2_out), .in1(A1__RI), .out(multiplexer_8_out), .sel(A1));  // open: en
  Multiplexer #(.width(24)) multiplexer_9 (
    .in0(multiplexer_3_out), .in1(iA1_imm), .out(multiplexer_9_out), .sel(A1));  // open: en
  Multiplexer #(.width(4)) multiplexer_10 (
    .in0(multiplexer_5_out), .in1(4'b0000), .out(multiplexer_10_out), .sel(A1));  // open: en
  Multiplexer #(.width(4)) multiplexer_11 (.in0(4'b0000), .in1(multiplexer_10_out), .out(RD), .sel(CQ));  // open: en
  Multiplexer #(.width(4)) multiplexer_12 (.in0(4'b0000), .in1(multiplexer_7_out), .out(RS), .sel(CQ));  // open: en
  Multiplexer #(.width(4)) multiplexer_13 (
    .in0(multiplexer_8_out), .in1(4'b0000), .out(multiplexer_13_out), .sel(imm));  // open: en
  Multiplexer #(.width(24)) multiplexer_14 (
    .in0({24{1'b0}}), .in1(multiplexer_9_out), .out(multiplexer_14_out), .sel(imm));  // open: en
  Multiplexer #(.width(4)) multiplexer_15 (.in0(4'b0000), .in1(multiplexer_13_out), .out(RI), .sel(CQ));  // open: en
  Multiplexer #(.width(24)) multiplexer_16 (
    .in0({24{1'b0}}), .in1(multiplexer_14_out), .out(Immediate), .sel(CQ));  // open: en

  // Notes on the sheet:
  //   inputs
  //   instruction selectors
  //   12th instruction selector
  //   13th instruction selector
  //   14th instruction selector
  //   15th instruction selector
  //   non immediates
  //   immediates
  //   A2/A3 switches
  //   Choose %RI
  //   outputs
  //   Choose %RD
  //   Choose %RS
  //   Choose immediate
endmodule

module decoder (
  input  [31:0] inst,
  output [3:0] opcode,
  output [2:0] CQ,
  output Imm,
  output [23:0] nxtInst
);


  assign CQ = inst[27:25];
  assign Imm = inst[24];
  assign nxtInst = inst[23:0];
  assign opcode = inst[31:28];
endmodule

module Adder_Logic (
  input  [23:0] pc,
  input  [23:0] sel_imm,
  input  [3:0] opcode,
  output [23:0] next_pc
);

  wire _15, bitselector_1_out, bitselector_2_out, bitselector_3_out, bitselector_4_out;
  wire [23:0] adder_1_out;

  BitSelector #(.width(4)) bitselector_1 (.in(opcode), .out(bitselector_1_out), .sel(2'b11));
  BitSelector #(.width(4)) bitselector_2 (.in(opcode), .out(bitselector_2_out), .sel(2'b10));
  BitSelector #(.width(4)) bitselector_3 (.in(opcode), .out(bitselector_3_out), .sel(2'b01));
  BitSelector #(.width(4)) bitselector_4 (.in(opcode), .out(bitselector_4_out), .sel(2'b00));
  and and_1 (_15, bitselector_1_out, bitselector_2_out, bitselector_3_out, bitselector_4_out);
  Adder #(.width(24)) adder_1 (.a(pc), .b(24'h1), .out(adder_1_out));  // open: cin, cout
  Multiplexer #(.width(24)) multiplexer_1 (.in0(adder_1_out), .in1(sel_imm), .out(next_pc), .sel(_15));  // open: en

  // Other names for the same wires on the sheet: imm[23:0] = sel_imm; op[3:0] = opcode
endmodule

module control (
  input  [3:0] opcode,
  output jump,
  output link,
  output reg_write,
  output memWrite,
  output load,
  output comp
);

  wire _11, _12, _13, bitselector_1_out, bitselector_2_out, bitselector_3_out, bitselector_4_out,
       bitselector_5_out, bitselector_6_out, bitselector_7_out, bitselector_8_out, bitselector_9_out,
       bitselector_10_out, bitselector_11_out, bitselector_12_out, bitselector_13_out, bitselector_14_out,
       bitselector_15_out, bitselector_16_out, bitselector_17_out, bitselector_18_out, bitselector_19_out,
       bitselector_20_out, bitselector_21_out, bitselector_22_out, bitselector_23_out, bitselector_24_out,
       bitselector_25_out, bitselector_26_out, bitselector_27_out, bitselector_28_out, not_1_out, not_2_out,
       not_3_out, not_4_out, not_5_out, not_6_out, not_7_out, not_8_out, or_1_out;

  BitSelector #(.width(4)) bitselector_1 (.in(opcode), .out(bitselector_1_out), .sel(2'b11));
  BitSelector #(.width(4)) bitselector_2 (.in(opcode), .out(bitselector_2_out), .sel(2'b10));
  not not_1 (not_1_out, bitselector_3_out);
  BitSelector #(.width(4)) bitselector_3 (.in(opcode), .out(bitselector_3_out), .sel(2'b01));
  BitSelector #(.width(4)) bitselector_4 (.in(opcode), .out(bitselector_4_out), .sel(2'b00));
  not not_2 (not_2_out, bitselector_4_out);
  BitSelector #(.width(4)) bitselector_5 (.in(opcode), .out(bitselector_5_out), .sel(2'b11));
  BitSelector #(.width(4)) bitselector_6 (.in(opcode), .out(bitselector_6_out), .sel(2'b10));
  not not_3 (not_3_out, bitselector_7_out);
  BitSelector #(.width(4)) bitselector_7 (.in(opcode), .out(bitselector_7_out), .sel(2'b01));
  BitSelector #(.width(4)) bitselector_8 (.in(opcode), .out(bitselector_8_out), .sel(2'b00));
  BitSelector #(.width(4)) bitselector_9 (.in(opcode), .out(bitselector_9_out), .sel(2'b11));
  BitSelector #(.width(4)) bitselector_10 (.in(opcode), .out(bitselector_10_out), .sel(2'b10));
  BitSelector #(.width(4)) bitselector_11 (.in(opcode), .out(bitselector_11_out), .sel(2'b01));
  BitSelector #(.width(4)) bitselector_12 (.in(opcode), .out(bitselector_12_out), .sel(2'b00));
  not not_4 (not_4_out, bitselector_12_out);
  BitSelector #(.width(4)) bitselector_13 (.in(opcode), .out(bitselector_13_out), .sel(2'b11));
  BitSelector #(.width(4)) bitselector_14 (.in(opcode), .out(bitselector_14_out), .sel(2'b10));
  BitSelector #(.width(4)) bitselector_15 (.in(opcode), .out(bitselector_15_out), .sel(2'b01));
  BitSelector #(.width(4)) bitselector_16 (.in(opcode), .out(bitselector_16_out), .sel(2'b00));
  BitSelector #(.width(4)) bitselector_17 (.in(opcode), .out(bitselector_17_out), .sel(2'b11));
  BitSelector #(.width(4)) bitselector_18 (.in(opcode), .out(bitselector_18_out), .sel(2'b10));
  not not_5 (not_5_out, bitselector_18_out);
  BitSelector #(.width(4)) bitselector_19 (.in(opcode), .out(bitselector_19_out), .sel(2'b01));
  BitSelector #(.width(4)) bitselector_20 (.in(opcode), .out(bitselector_20_out), .sel(2'b00));
  and and_1 (_12, bitselector_1_out, bitselector_2_out, not_1_out, not_2_out);
  and and_2 (_13, bitselector_5_out, bitselector_6_out, not_3_out, bitselector_8_out);
  and and_3 (link, bitselector_9_out, bitselector_10_out, bitselector_11_out, not_4_out);
  and and_4 (jump, bitselector_13_out, bitselector_14_out, bitselector_15_out, bitselector_16_out);
  and and_5 (_11, bitselector_17_out, not_5_out, bitselector_19_out, bitselector_20_out);
  or or_1 (or_1_out, _11, _12, _13, jump);
  BitSelector #(.width(4)) bitselector_21 (.in(opcode), .out(bitselector_21_out), .sel(2'b11));
  BitSelector #(.width(4)) bitselector_22 (.in(opcode), .out(bitselector_22_out), .sel(2'b10));
  not not_6 (not_6_out, bitselector_22_out);
  BitSelector #(.width(4)) bitselector_23 (.in(opcode), .out(bitselector_23_out), .sel(2'b01));
  BitSelector #(.width(4)) bitselector_24 (.in(opcode), .out(bitselector_24_out), .sel(2'b00));
  BitSelector #(.width(4)) bitselector_25 (.in(opcode), .out(bitselector_25_out), .sel(2'b11));
  BitSelector #(.width(4)) bitselector_26 (.in(opcode), .out(bitselector_26_out), .sel(2'b10));
  not not_7 (not_7_out, bitselector_26_out);
  BitSelector #(.width(4)) bitselector_27 (.in(opcode), .out(bitselector_27_out), .sel(2'b01));
  not not_8 (not_8_out, bitselector_28_out);
  BitSelector #(.width(4)) bitselector_28 (.in(opcode), .out(bitselector_28_out), .sel(2'b00));
  or or_2 (comp, _12, _13);
  not not_9 (reg_write, or_1_out);
  and and_6 (memWrite, bitselector_21_out, not_6_out, bitselector_23_out, bitselector_24_out);
  and and_7 (load, bitselector_25_out, not_7_out, bitselector_27_out, not_8_out);

  // Other names for the same wires on the sheet: _14 = link; _15 = jump; op[3:0] = opcode

  // Notes on the sheet:
  //   instruction selectors
  //   12th instruction selector
  //   13th instruction selector
  //   14th instruction selector
  //   15th instruction selector
  //   11th instruction selector
  //   Jump Control
  //   Link Control
  //   Reg Write Control
  //   Store Control
  //   Load Control
  //   Comparison Control
endmodule
