// Logisim project REG.circ as structural Verilog: 3 circuits, main circuit Ida Register File
// Register File
module Ida_Register_File (
  input  [3:0] Read_Reg_1,
  input  [3:0] Read_Reg_2,
  input  [3:0] Write_Reg,
  input  [23:0] Write_Value,
  input  Reg_Write,
  input  Clock,
  output [23:0] Reg_1_Value,
  output [23:0] Reg_2_Value,
  output [23:0] Reg_3_Value,
  output [23:0] r00,
  output [23:0] r01,
  output [23:0] r02,
  output [23:0] r03,
  output [23:0] r04,
  output [23:0] r05,
  output [23:0] r06,
  output [23:0] r07,
  output [23:0] r08,
  output [23:0] r09,
  output [23:0] r10,
  output [23:0] r11,
  output [23:0] r12,
  output [23:0] r13,
  output [23:0] r14,
  output [23:0] r15
);

  wire [23:0] new_R00, new_R01, new_R02, new_R03, new_R04, new_R05, new_R06, new_R07, new_R08, new_R09,
       new_R10, new_R11, new_R12, new_R13, new_R14, new_R15;

  // Probe on Read_Reg_1
  // Probe on Read_Reg_2
  // Probe on Write_Reg
  // Probe on Write_Value
  // Probe on Reg_Write
  // Probe on Clock
  // Probe on Reg_1_Value
  // Probe on Reg_2_Value
  // Probe on Reg_3_Value
  // Probe on r00
  // Probe on r01
  // Probe on r02
  // Probe on r03
  // Probe on r04
  // Probe on r05
  // Probe on r06
  // Probe on r07
  // Probe on r08
  // Probe on r09
  // Probe on r10
  // Probe on r11
  // Probe on r12
  // Probe on r13
  // Probe on r14
  // Probe on r15
  writeback writeback_1 (
    .R00(r00), .R01(r01), .R02(r02), .R03(r03), .R04(r04), .R05(r05), .R06(r06), .R07(r07), .R08(r08),
    .R09(r09), .R10(r10), .R11(r11), .R12(r12), .R13(r13), .R14(r14), .R15(r15), .write_val(Write_Value),
    .write_back(Reg_Write), .select_reg(Write_Reg), .new_R00(new_R00), .new_R01(new_R01), .new_R02(new_R02),
    .new_R03(new_R03), .new_R04(new_R04), .new_R05(new_R05), .new_R06(new_R06), .new_R07(new_R07),
    .new_R08(new_R08), .new_R09(new_R09), .new_R10(new_R10), .new_R11(new_R11), .new_R12(new_R12),
    .new_R13(new_R13), .new_R14(new_R14), .new_R15(new_R15));
  Register #(.width(24)) u_R00 (.D(new_R00), .Q(r00), .clk(Clock));  // open: en, clr
  Register #(.width(24)) u_R04 (.D(new_R04), .Q(r04), .clk(Clock));  // open: en, clr
  Register #(.width(24)) u_R08 (.D(new_R08), .Q(r08), .clk(Clock));  // open: en, clr
  Register #(.width(24)) u_R12 (.D(new_R12), .Q(r12), .clk(Clock));  // open: en, clr
  Register #(.width(24)) u_R01 (.D(new_R01), .Q(r01), .clk(Clock));  // open: en, clr
  Register #(.width(24)) u_R05 (.D(new_R05), .Q(r05), .clk(Clock));  // open: en, clr
  Register #(.width(24)) u_R09 (.D(new_R09), .Q(r09), .clk(Clock));  // open: en, clr
  Register #(.width(24)) u_R13 (.D(new_R13), .Q(r13), .clk(Clock));  // open: en, clr
  Register #(.width(24)) u_R02 (.D(new_R02), .Q(r02), .clk(Clock));  // open: en, clr
  Register #(.width(24)) u_R06 (.D(new_R06), .Q(r06), .clk(Clock));  // open: en, clr
  Register #(.width(24)) u_R10 (.D(new_R10), .Q(r10), .clk(Clock));  // open: en, clr
  Register #(.width(24)) u_R14 (.D(new_R14), .Q(r14), .clk(Clock));  // open: en, clr
  Register #(.width(24)) u_R03 (.D(new_R03), .Q(r03), .clk(Clock));  // open: en, clr
  Register #(.width(24)) u_R07 (.D(new_R07), .Q(r07), .clk(Clock));  // open: en, clr
  Register #(.width(24)) u_R11 (.D(new_R11), .Q(r11), .clk(Clock));  // open: en, clr
  Register #(.width(24)) u_R15 (.D(new_R15), .Q(r15), .clk(Clock));  // open: en, clr
  select_reg select_reg_1 (
    .R00(r00), .R01(r01), .R02(r02), .R03(r03), .R04(r04), .R05(r05), .R06(r06), .R07(r07), .R08(r08),
    .R09(r09), .R10(r10), .R11(r11), .R12(r12), .R13(r13), .R14(r14), .R15(r15), .reg1Read(Read_Reg_1),
    .reg2Read(Read_Reg_2), .reg3Read(Write_Reg), .reg1Val(Reg_1_Value), .reg2Val(Reg_2_Value),
    .reg3Val(Reg_3_Value));

  // Other names for the same wires on the sheet: clk = Clock; reg1Read[3:0] = Read_Reg_1; reg1Val[23:0] = Reg_1_Value;
  //   reg2Read[3:0] = Read_Reg_2; reg2Val[23:0] = Reg_2_Value; reg3Val[23:0] = Reg_3_Value;
  //   reg3Write[3:0] = Write_Reg; write = Reg_Write; writeVal[23:0] = Write_Value

  // Notes on the sheet:
  //   INPUT PINS
  //   INPUT PROBES
  //   OUTPUT PROBES
  //   OUTPUT PINS
  //   DO NOT MOVE/ADD/CHANGE ANY INPUT OR OUTPUT PINS!
endmodule

module writeback (
  input  [23:0] R00,
  input  [23:0] R01,
  input  [23:0] R02,
  input  [23:0] R03,
  input  [23:0] R04,
  input  [23:0] R05,
  input  [23:0] R06,
  input  [23:0] R07,
  input  [23:0] R08,
  input  [23:0] R09,
  input  [23:0] R10,
  input  [23:0] R11,
  input  [23:0] R12,
  input  [23:0] R13,
  input  [23:0] R14,
  input  [23:0] R15,
  input  [23:0] write_val,
  input  write_back,
  input  [3:0] select_reg,
  output [23:0] new_R00,
  output [23:0] new_R01,
  output [23:0] new_R02,
  output [23:0] new_R03,
  output [23:0] new_R04,
  output [23:0] new_R05,
  output [23:0] new_R06,
  output [23:0] new_R07,
  output [23:0] new_R08,
  output [23:0] new_R09,
  output [23:0] new_R10,
  output [23:0] new_R11,
  output [23:0] new_R12,
  output [23:0] new_R13,
  output [23:0] new_R14,
  output [23:0] new_R15
);

  wire R00_t, R01_t, R02_t, R03_t, R04_t, R05_t, R06_t, R07_t, R08_t, R09_t, R10_t, R11_t, R12_t, R13_t,
       R14_t, R15_t;

  Multiplexer #(.width(24)) multiplexer_1 (.in0(R00), .in1(write_val), .out(new_R00), .sel(R00_t));  // open: en
  Multiplexer #(.width(24)) multiplexer_2 (.in0(R01), .in1(write_val), .out(new_R01), .sel(R01_t));  // open: en
  Multiplexer #(.width(24)) multiplexer_3 (.in0(R02), .in1(write_val), .out(new_R02), .sel(R02_t));  // open: en
  Multiplexer #(.width(24)) multiplexer_4 (.in0(R03), .in1(write_val), .out(new_R03), .sel(R03_t));  // open: en
  Multiplexer #(.width(24)) multiplexer_5 (.in0(R04), .in1(write_val), .out(new_R04), .sel(R04_t));  // open: en
  Multiplexer #(.width(24)) multiplexer_6 (.in0(R05), .in1(write_val), .out(new_R05), .sel(R05_t));  // open: en
  Multiplexer #(.width(24)) multiplexer_7 (.in0(R06), .in1(write_val), .out(new_R06), .sel(R06_t));  // open: en
  Multiplexer #(.width(24)) multiplexer_8 (.in0(R07), .in1(write_val), .out(new_R07), .sel(R07_t));  // open: en
  Multiplexer #(.width(24)) multiplexer_9 (.in0(R08), .in1(write_val), .out(new_R08), .sel(R08_t));  // open: en
  Multiplexer #(.width(24)) multiplexer_10 (.in0(R09), .in1(write_val), .out(new_R09), .sel(R09_t));  // open: en
  Multiplexer #(.width(24)) multiplexer_11 (.in0(R10), .in1(write_val), .out(new_R10), .sel(R10_t));  // open: en
  Multiplexer #(.width(24)) multiplexer_12 (.in0(R11), .in1(write_val), .out(new_R11), .sel(R11_t));  // open: en
  Multiplexer #(.width(24)) multiplexer_13 (.in0(R12), .in1(write_val), .out(new_R12), .sel(R12_t));  // open: en
  Multiplexer #(.width(24)) multiplexer_14 (.in0(R13), .in1(write_val), .out(new_R13), .sel(R13_t));  // open: en
  Multiplexer #(.width(24)) multiplexer_15 (.in0(R14), .in1(write_val), .out(new_R14), .sel(R14_t));  // open: en
  Multiplexer #(.width(24)) multiplexer_16 (.in0(R15), .in1(write_val), .out(new_R15), .sel(R15_t));  // open: en
  Demultiplexer #(.select(4)) demultiplexer_1 (
    .out0(R00_t), .out1(R01_t), .out2(R02_t), .out3(R03_t), .out4(R04_t), .out5(R05_t), .out6(R06_t),
    .out7(R07_t), .out8(R08_t), .out9(R09_t), .out10(R10_t), .out11(R11_t), .out12(R12_t), .out13(R13_t),
    .out14(R14_t), .out15(R15_t), .in(write_back), .sel(select_reg));  // open: en
endmodule

module select_reg (
  input  [23:0] R00,
  input  [23:0] R01,
  input  [23:0] R02,
  input  [23:0] R03,
  input  [23:0] R04,
  input  [23:0] R05,
  input  [23:0] R06,
  input  [23:0] R07,
  input  [23:0] R08,
  input  [23:0] R09,
  input  [23:0] R10,
  input  [23:0] R11,
  input  [23:0] R12,
  input  [23:0] R13,
  input  [23:0] R14,
  input  [23:0] R15,
  input  [3:0] reg1Read,
  input  [3:0] reg2Read,
  input  [3:0] reg3Read,
  output [23:0] reg1Val,
  output [23:0] reg2Val,
  output [23:0] reg3Val
);

  Multiplexer #(.select(4), .width(24)) multiplexer_1 (
    .in0(R00), .in1(R01), .in2(R02), .in3(R03), .in4(R04), .in5(R05), .in6(R06), .in7(R07), .in8(R08),
    .in9(R09), .in10(R10), .in11(R11), .in12(R12), .in13(R13), .in14(R14), .in15(R15), .out(reg1Val),
    .sel(reg1Read));  // open: en
  Multiplexer #(.select(4), .width(24)) multiplexer_2 (
    .in0(R00), .in1(R01), .in2(R02), .in3(R03), .in4(R04), .in5(R05), .in6(R06), .in7(R07), .in8(R08),
    .in9(R09), .in10(R10), .in11(R11), .in12(R12), .in13(R13), .in14(R14), .in15(R15), .out(reg2Val),
    .sel(reg2Read));  // open: en
  Multiplexer #(.select(4), .width(24)) multiplexer_3 (
    .in0(R00), .in1(R01), .in2(R02), .in3(R03), .in4(R04), .in5(R05), .in6(R06), .in7(R07), .in8(R08),
    .in9(R09), .in10(R10), .in11(R11), .in12(R12), .in13(R13), .in14(R14), .in15(R15), .out(reg3Val),
    .sel(reg3Read));  // open: en
endmodule
